# Fritzing sketch sonar3_battery_L298motor (saved by Fritzing 0.9.10b)
breadboards: 1

parts:
  부품1 = Arduino Mega 2560 (Rev3)
  HC-SR04_Sensor_1 = HC-SR04 Ultrasonic Distance Sensor
  S1 = H-Bridge with L298N
  HC-SR04_Sensor_2 = HC-SR04 Ultrasonic Distance Sensor
  HC-SR04_Sensor_3 = HC-SR04 Ultrasonic Distance Sensor
  VCC2 = Battery

nets:
  N1: 부품1.D13_PWM, S1.ENB
  N2: 부품1.D12_PWM, S1.IN4
  N3: 부품1.D11_PWM, S1.IN3
  N4: 부품1.D10_PWM, S1.IN2
  N5: 부품1.D9_PWM, S1.IN1
  N6: 부품1.D8_PWM, S1.ENA
  VCC: 부품1.5V, HC-SR04_Sensor_1.VCC, S1.5V, HC-SR04_Sensor_2.VCC, HC-SR04_Sensor_3.VCC
  GND: 부품1.GND, HC-SR04_Sensor_1.GND, S1.GND, HC-SR04_Sensor_2.GND, HC-SR04_Sensor_3.GND, VCC2.-
  N7: 부품1.D2_PWM, HC-SR04_Sensor_1.TRIG
  N8: 부품1.D3_PWM, HC-SR04_Sensor_1.ECHO
  N9: 부품1.D4_PWM, HC-SR04_Sensor_2.TRIG
  N10: 부품1.D5_PWM, HC-SR04_Sensor_2.ECHO
  N11: 부품1.D6_PWM, HC-SR04_Sensor_3.TRIG
  N12: 부품1.D7_PWM, HC-SR04_Sensor_3.ECHO
  N13: S1.12V, VCC2.+

custom parts:
  H-Bridge with L298N: h-bridge
  Battery: Your standard 2x 18650 battery pack (7,4 Volts)
